# Fritzing sketch Schematic_Tutorial_1.0 (saved by Fritzing 0.9.2b)
breadboards: 1

parts:
  R1 = Rotary Potentiometer (Small) [maximum_resistance=100kΩ package=THT]
  Part1 = Arduino Nano (Rev3.0)

nets:
  N1: R1.leg1, Part1.GND
  N2: R1.wiper, Part1.A5
  N3: R1.leg2, Part1.5V
