# Fritzing sketch Schematic_Tutorial_1.2 (saved by Fritzing 0.9.2b)
breadboards: 1

parts:
  R2 = Rotary Potentiometer (Small) [maximum_resistance=100kΩ package=THT]
  Part2 = Arduino Nano (Rev3.0)
  LED1 = LED - 5mm [color="Red (633nm)" package="5 mm [THT]"]
  R3 = Resistor [tolerance=±5% resistance=220 package=THT]

nets:
  N1: R2.leg1, Part2.GND, LED1.cathode
  N2: R2.wiper, Part2.A5
  N3: R2.leg2, Part2.5V
  N4: Part2.D11/MOSI, R3.Pin_0
  N5: LED1.anode, R3.Pin_1
